# Fritzing sketch IntervaluinoPlus (saved by Fritzing 0.7.4b)
breadboards: 1

parts:
  Arduino1 = Arduino
  S1 = Pushbutton [part_number=RIGHT package="[THT]"]
  S2 = Pushbutton [part_number=LEFT package="[THT]"]
  S3 = Pushbutton [part_number=UP package="[THT]"]
  S4 = Pushbutton [part_number=DOWN package="[THT]"]
  R1 = Resistor [tolerance=±5% resistance=10k package=THT]
  R2 = Resistor [tolerance=±5% resistance=10k package=THT]
  R3 = Resistor [tolerance=±5% resistance=10k package=THT]
  R4 = Resistor [tolerance=±5% resistance=10k package=THT]
  COM-09764/5/6/7 = mystery part, 3 pins [chip_label=COM-0976X spacing=300mil]
  U1 = Optocoupler [package=THT]
  R5 = Resistor [tolerance=±5% resistance=330 package=THT]
  TRS1 = Audio Jack (TRS) 3.5mm [package="4Ucon 08780 [THT]"]

nets:
  N1: Arduino1.GND, R1.Pin_1, R2.Pin_1, R3.Pin_1, R4.Pin_1, COM-09764/5/6/7.pin1, U1.Pin_2
  N2: Arduino1.D9, R5.Pin_0
  N3: Arduino1.D8, S4.Pin_1, S4.Pin_2, R3.Pin_0
  N4: Arduino1.D7, S3.Pin_1, S3.Pin_2, R4.Pin_0
  N5: Arduino1.D6, S2.Pin_1, S2.Pin_2, R2.Pin_0
  N6: Arduino1.D5, S1.Pin_1, S1.Pin_2, R1.Pin_0
  N7: Arduino1.D3, COM-09764/5/6/7.pin3
  N8: Arduino1.+5V, S1.Pin_3, S1.Pin_4, S2.Pin_3, S2.Pin_4, S3.Pin_3, S3.Pin_4, S4.Pin_3, S4.Pin_4, COM-09764/5/6/7.pin2
  N9: U1.Pin_1, R5.Pin_1
  N10: U1.Pin_4, TRS1.Sleeve
  N11: U1.Pin_5, TRS1.Tip
